# Fritzing sketch Diagrama_de_Conexión_KUKO_DELTA_rev3 (saved by Fritzing 1.0.4)

parts:
  U1 = ESP32-38PinWide [part_number=ESP32-38PinWide]
  A1 = AS5600 module
  A2 = AS5600 module
  A3 = AS5600 module
  A6 = DM860A Stepper Motor Driver
  S1 = Pushbutton [package="[THT]"]
  S2 = Pushbutton [package="[THT]"]
  S3 = Pushbutton [package="[THT]"]
  V2 = DC Power Supply [voltage=12V internal_resistance=1Ω max_current=0.1A]
  V3 = DC Power Supply [voltage=12V internal_resistance=1Ω max_current=0.1A]
  V4 = DC Power Supply [voltage=12V internal_resistance=1Ω max_current=0.1A]
  M4 = DC Motor [voltage_(max)=6V voltage_(min)=3V]
  WATER_PUMP1 = water pump/motor
  IC1 = DRV8833 Motor Driver Board (MJKDZ) [package="DIP (Dual Inline) [THT]"]
  Componente1 = IFR520 MOS module [package=THT]
  A7 = Sparkfun tca9548a
  M7 = Stepper Motor - Bipolar
  A8 = DM860A Stepper Motor Driver
  M8 = Stepper Motor - Bipolar
  A9 = DM860A Stepper Motor Driver
  M9 = Stepper Motor - Bipolar
  U6 = TXS0108 [part_number=TXS0108EPW package=TSSOP]
  J2 = JST-VHR-3N [part_number=JST-VHR-3N package=THT]
  J3 = JST-VHR-3N [part_number=JST-VHR-3N package=THT]
  J4 = JST-VHR-3N [part_number=JST-VHR-3N package=THT]
  J5 = JST-VHR-3N [part_number=JST-VHR-3N package=THT]
  J6 = JST-VHR-3N [part_number=JST-VHR-3N package=THT]
  J7 = JST-VHR-3N [part_number=JST-VHR-3N package=THT]
  V5 = DC Power Supply [voltage=12V internal_resistance=1Ω max_current=0.1A]
  J8 = JST-VHR-3N [part_number=JST-VHR-3N package=THT]
  J9 = STARBOARD_GND [package=starboard_ground_small2]
  J10 = STARBOARD_GND [package=starboard_ground_small2]
  J11 = STARBOARD_GND [package=starboard_ground_small2]
  J12 = STARBOARD_GND [package=starboard_ground_small]
  J13 = JST-VHR-3N [part_number=JST-VHR-3N package=THT]
  J14 = STARBOARD_GND [package=starboard_ground_small2]
  J15 = STARBOARD_GND [package=starboard_ground_small2]
  J16 = STARBOARD_GND [package=starboard_ground_small2]
  J17 = STARBOARD_GND [package=starboard_ground_small]
  J18 = JST-VHR-3N [part_number=JST-VHR-3N package=THT]
  J19 = STARBOARD_GND [package=starboard_ground_small]
  J20 = STARBOARD_GND [package=starboard_ground_small]
  J21 = STARBOARD_GND [package=starboard_ground_small]
  J22 = STARBOARD_GND [package=starboard_ground_small]
  J23 = STARBOARD_GND [package=starboard_ground_small]
  Boost_Convertor1 = Boost Convertor [part_number=XL6009E1 package=THT]
  J24 = STARBOARD_GND [package=starboard_ground_small]
  J25 = STARBOARD_GND [package=starboard_ground_small]
  J26 = STARBOARD_GND [package=starboard_ground_small]
  J27 = STARBOARD_GND [package=starboard_ground_small]
  J28 = STARBOARD_GND [package=starboard_ground_small]
  J29 = JST-VHR-3N [part_number=JST-VHR-3N package=THT]
  J30 = STARBOARD_GND [package=starboard_ground_small]
  J31 = STARBOARD_GND [package=starboard_ground_small]
  J32 = STARBOARD_GND [package=starboard_ground_small]
  J33 = STARBOARD_GND [package=starboard_ground_small]
  J34 = STARBOARD_GND [package=starboard_ground_small]
  J35 = STARBOARD_GND [package=starboard_ground_small]
  WeMos_D1_Mini_Relay_Shield_V1 = WeMos D1 Mini Relay Shield V2
  J36 = JST-VHR-3N [part_number=JST-VHR-3N package=THT]
  J37 = STARBOARD_GND [package=starboard_ground_small]
  F1 = Fan - Ventilador [package=THT]
  A10 = RGB Strip LED
  J38 = STARBOARD_GND [package=starboard_ground_small]
  J39 = STARBOARD_GND [package=starboard_ground_small]

nets:
  N1: U1.GPIO32, U6.A6
  N2: U1.GPIO33, U6.A5
  N3: U1.GPIO25, U6.A4
  N4: U1.GPIO26, U6.A3
  N5: U1.GPIO27, U6.A2
  N6: U1.GPIO14, U6.A1
  N7: U1.GPIO13, J36.pin3, J36.pin_6
  N8: U1.GPIO16, S1.Pin_3
  N9: U1.GPIO17, S2.Pin_3
  N10: U1.GPIO18, S3.Pin_3
  N11: U1.GPIO19, IC1.pin6
  N12: U1.GPIO21, A7.Pin_39
  N13: U1.GPIO22, A7.Pin_40
  N14: U1.GPIO23, Componente1.pin1
  N15: A1.Pin_1, A2.Pin_1, A3.Pin_1, J29.pin1, J29.pin_4
  N16: A1.Pin_3, J33.MOUNT
  N17: A1.Pin_5, A7.Pin_11
  N18: A1.Pin_6, A7.Pin_12
  N19: A1.Pin_7, J32.MOUNT
  N20: A2.Pin_3, J34.MOUNT
  N21: A2.Pin_5, A7.Pin_7
  N22: A2.Pin_6, A7.Pin_8
  N23: A2.Pin_7, J31.MOUNT
  N24: A3.Pin_3, J35.MOUNT
  N25: A3.Pin_5, A7.Pin_3
  N26: A3.Pin_6, A7.Pin_4
  N27: A3.Pin_7, J30.MOUNT
  N28: A6.B-, M7.D
  N29: A6.B+, M7.B
  N30: A6.A-, M7.C
  N31: A6.A+, M7.A
  N32: A6.VDC, J8.pin3, J8.pin_6
  N33: A6.GND, J11.MOUNT
  N34: A6.ENBL-(ENB), U6.B7, J7.pin2, J7.pin_5
  N35: A6.ENBL+(+5V), J4.pin_6
  N36: A6.DIR-(DIR), U6.B6
  N37: A6.DIR+(+5V), U6.VccB, J4.pin2, J4.pin_5, J5.pin3, J5.pin_6
  N38: A6.PUL-(PUL), U6.B3
  N39: A6.PUL+(+5V), J4.pin_4
  N40: S1.Pin_1, J16.MOUNT
  N41: S2.Pin_1, J15.MOUNT
  N42: S3.Pin_1, J14.MOUNT
  N43: V2.Pin_2, U6.OE, J13.pin2, J13.pin_5
  N44: V2.Pin_1, J20.MOUNT
  N45: V3.Pin_2, J6.pin2, J6.pin_5, Boost_Convertor1.Positive_Input, WeMos_D1_Mini_Relay_Shield_V1.5V
  N46: V3.Pin_1, J21.MOUNT
  N47: V4.Pin_2, J18.pin2
  N48: V4.Pin_1, J22.MOUNT
  N49: M4.pin_1, IC1.pin11
  N50: M4.pin_2, IC1.pin10
  N51: WATER_PUMP1.pin_1, Componente1.pin5
  N52: WATER_PUMP1.pin_2, Componente1.pin4
  N53: IC1.pin3, J26.MOUNT
  N54: IC1.pin4, Boost_Convertor1.Positive_Output
  N55: IC1.pin5, J27.MOUNT
  N56: Componente1.pin2, J6.pin3, J6.pin_6
  N57: Componente1.pin3, J17.MOUNT
  N58: Componente1.pin6, J18.pin3, J18.pin_6
  N59: Componente1.pin7, J19.MOUNT
  N60: A7.Pin_1, A7.Pin_37, J28.MOUNT
  N61: A7.Pin_38, J29.pin_6
  N62: A8.B-, M8.D
  N63: A8.B+, M8.B
  N64: A8.A-, M8.C
  N65: A8.A+, M8.A
  N66: A8.VDC, V5.Pin_2, J8.pin2, J8.pin_5
  N67: A8.GND, J10.MOUNT
  N68: A8.ENBL-(ENB), J7.pin_4
  N69: A8.ENBL+(+5V), J3.pin_6
  N70: A8.DIR-(DIR), U6.B5
  N71: A8.DIR+(+5V), J3.pin2, J3.pin_5, J5.pin2, J5.pin_5, J6.pin1, J6.pin_4
  N72: A8.PUL-(PUL), U6.B2
  N73: A8.PUL+(+5V), J3.pin_4
  N74: A9.B-, M9.D
  N75: A9.B+, M9.B
  N76: A9.A-, M9.C
  N77: A9.A+, M9.A
  N78: A9.VDC, J8.pin1, J8.pin_4
  N79: A9.GND, J9.MOUNT
  N80: A9.ENBL-(ENB), J7.pin_6
  N81: A9.ENBL+(+5V), J2.pin_6
  N82: A9.DIR-(DIR), U6.B4
  N83: A9.DIR+(+5V), J2.pin2, J2.pin_5, J5.pin1, J5.pin_4
  N84: A9.PUL-(PUL), U6.B1
  N85: A9.PUL+(+5V), J2.pin_4
  N86: U6.VccA, J13.pin1, J13.pin_4
  N87: U6.A7, J36.pin1, J36.pin_4
  N88: U6.GND, J12.MOUNT
  N89: V5.Pin_1, J23.MOUNT
  N90: J13.pin_6, J29.pin2
  N91: J18.pin_4, WeMos_D1_Mini_Relay_Shield_V1.COM
  N92: Boost_Convertor1.Negative_Input, J24.MOUNT
  N93: Boost_Convertor1.Negative_Output, J25.MOUNT
  N94: WeMos_D1_Mini_Relay_Shield_V1.D4, J36.pin2, J36.pin_5
  N95: WeMos_D1_Mini_Relay_Shield_V1.G, J37.MOUNT
  N96: WeMos_D1_Mini_Relay_Shield_V1.NO, F1.5V, A10.Common_Connect
  N97: F1.GND, J38.MOUNT
  N98: A10.Green_Connect, J39.MOUNT

notes:
  Fuente 5V
  Fuente 3.3V
  Fuente 12V
  Fuente 48V
  MOTOR 1
  MOTOR 2
  MOTOR 3
  FC1
  FC2
  FC3
  BOMBA NEUMÁTICA
  MOTORREDUCTOR DC CINTA (70RPM)
  WEBCAM USB
  STEP-UP XL6009E1
  SDA
  SCL
  0,1 y 2 a GND
  dir. (x70)
  SD: Data
  SC: Clock
  D4= Signal

custom parts:
  ESP32-38PinWide: Generic 38-Pin ESP32 with wide format (only access to one side of pins on a breadboard) based on Stephen Lilley's HiLetgo ESP-WROOM-32 ESP32 ESP-32S Development Board.
  AS5600 module: .This module is mainly placed behind the stepper motor to obtain the rotation angle of the stepper motor.
  DM860A Stepper Motor Driver: DM860A is a type of two-phase hybrid stepping motor driver, The drive voltage of which is from 24VDC to 80VDC. It is designed for use with 2-phase hybrid stepper motor of all kinds with 57mm to 110mm outside diameter and less than 8.0A phase current. Mar 2023: Correct pcb layerId as the part won't save correctly in a .fzz file as is.
  water pump/motor: WATER PUMP BY ARDUBLOCKTR
  DRV8833 Motor Driver Board (MJKDZ): A module made by MJKDZ, containg DRV8833 motor driver chip on PCB with 12-pin DIP 600mil footprint. Contains decoupling caps and an enable pad (J2). Does not bring out all IC pins. EEP = SLEEP input (needs pulling logic high to enable motors) ULT = FAULT output.
  Sparkfun tca9548a: Do you have too many sensors with the same I2C address? Put them on the SparkFun Qwiic Mux Breakout to get them all talking on the same bus! The Qwiic Mux Breakout enables communication with multiple I2C devices that have the same address that makes it simple to interface with.
  TXS0108: This 8-bit non-inverting translator uses two separate configurable power-supply rails. The A port tracks the VCCA pin supply voltage. The VCCA pin accepts any supply voltage between 1.2 V and 3.6 V. The B port tracks the VCCB pin supply voltage. The VCCB pin accepts any supply voltage between 1.65 V and 5.5 V. Two input supply pins allows for low Voltage bidirectional translation between any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
  Boost Convertor: DC to DC boost convertor
  Fan - Ventilador: Ventilador de 2 pines, se encuentra comunmente en computadoras de escritorio
  RGB Strip LED: A tri-color Strip LED with red, green and blue. Pin order: red - common cathode - blue - green
