# Fritzing sketch Diagrama_de_conexión (saved by Fritzing 1.0.4)

parts:
  U1 = ESP32-38PinWide [part_number=ESP32-38PinWide]
  A1 = AS5600 module
  A2 = AS5600 module
  A3 = AS5600 module
  A6 = DM860A Stepper Motor Driver
  S1 = Pushbutton [package="[THT]"]
  S2 = Pushbutton [package="[THT]"]
  S3 = Pushbutton [package="[THT]"]
  V2 = DC Power Supply [voltage=12V internal_resistance=1Ω max_current=0.1A]
  V3 = DC Power Supply [voltage=12V internal_resistance=1Ω max_current=0.1A]
  V4 = DC Power Supply [voltage=12V internal_resistance=1Ω max_current=0.1A]
  M4 = DC Motor [voltage_(max)=6V voltage_(min)=3V]
  WATER_PUMP1 = water pump/motor
  IC1 = DRV8833 Motor Driver Board (MJKDZ) [package="DIP (Dual Inline) [THT]"]
  Componente1 = IFR520 MOS module [package=THT]
  M7 = Stepper Motor - Bipolar
  A8 = DM860A Stepper Motor Driver
  M8 = Stepper Motor - Bipolar
  A9 = DM860A Stepper Motor Driver
  M9 = Stepper Motor - Bipolar
  J2 = JST-VHR-3N [part_number=JST-VHR-3N package=THT]
  J3 = JST-VHR-3N [part_number=JST-VHR-3N package=THT]
  J4 = JST-VHR-3N [part_number=JST-VHR-3N package=THT]
  J5 = JST-VHR-3N [part_number=JST-VHR-3N package=THT]
  J6 = JST-VHR-3N [part_number=JST-VHR-3N package=THT]
  J7 = JST-VHR-3N [part_number=JST-VHR-3N package=THT]
  V5 = DC Power Supply [voltage=12V internal_resistance=1Ω max_current=0.1A]
  J8 = JST-VHR-3N [part_number=JST-VHR-3N package=THT]
  J14 = STARBOARD_GND [package=starboard_ground_small2]
  J15 = STARBOARD_GND [package=starboard_ground_small2]
  J16 = STARBOARD_GND [package=starboard_ground_small2]
  J17 = STARBOARD_GND [package=starboard_ground_small]
  J18 = JST-VHR-3N [part_number=JST-VHR-3N package=THT]
  J20 = STARBOARD_GND [package=starboard_ground_small]
  J21 = STARBOARD_GND [package=starboard_ground_small]
  J22 = STARBOARD_GND [package=starboard_ground_small]
  Boost_Convertor1 = Boost Convertor [part_number=XL6009E1 package=THT]
  J24 = STARBOARD_GND [package=starboard_ground_small]
  J25 = STARBOARD_GND [package=starboard_ground_small]
  J26 = STARBOARD_GND [package=starboard_ground_small]
  J27 = STARBOARD_GND [package=starboard_ground_small]
  J29 = JST-VHR-3N [part_number=JST-VHR-3N package=THT]
  J30 = STARBOARD_GND [package=starboard_ground_small]
  J31 = STARBOARD_GND [package=starboard_ground_small]
  J32 = STARBOARD_GND [package=starboard_ground_small]
  J33 = STARBOARD_GND [package=starboard_ground_small]
  J34 = STARBOARD_GND [package=starboard_ground_small]
  J35 = STARBOARD_GND [package=starboard_ground_small]
  A10 = RGB Strip LED
  J39 = STARBOARD_GND [package=starboard_ground_small]
  J19 = STARBOARD_GND [package=starboard_ground_small]
  J44 = Camdenboss CTB0158-2 [part_number=CTB0158-2 package=THT]
  J45 = Camdenboss CTB0158-2 [part_number=CTB0158-2 package=THT]
  J46 = Camdenboss CTB0158-2 [part_number=CTB0158-2 package=THT]
  J47 = Camdenboss CTB0158-2 [part_number=CTB0158-2 package=THT]
  J48 = Camdenboss CTB0158-2 [part_number=CTB0158-2 package=THT]
  J49 = Camdenboss CTB0158-2 [part_number=CTB0158-2 package=THT]
  J50 = Camdenboss CTB0158-2 [part_number=CTB0158-2 package=THT]
  J51 = Camdenboss CTB0158-2 [part_number=CTB0158-2 package=THT]
  J52 = Camdenboss CTB0158-2 [part_number=CTB0158-2 package=THT]
  J53 = Camdenboss CTB0158-2 [part_number=CTB0158-2 package=THT]
  J54 = Camdenboss CTB0158-2 [part_number=CTB0158-2 package=THT]
  J55 = Camdenboss CTB0158-2 [part_number=CTB0158-2 package=THT]
  J56 = JST-VHR-3N [part_number=JST-VHR-3N package=THT]
  J57 = STARBOARD_GND [package=starboard_ground_small]
  J58 = STARBOARD_GND [package=starboard_ground_small]
  C1 = Capacitor [package=cap-pth-5mm]
  C2 = Capacitor [package=cap-pth-5mm]
  C3 = Capacitor [package=cap-pth-5mm]
  VALVE1 = Plastic Solenoid Valve
  C4 = Capacitor [package=cap-pth-5mm]
  C5 = Capacitor [package=cap-pth-5mm]
  C6 = Capacitor [package=cap-pth-5mm]

nets:
  N1: U1.GPIO39, A3.Pin_2, C1.2
  N2: U1.GPIO34, A2.Pin_2, C2.2
  N3: U1.GPIO35, A1.Pin_2, C3.2
  N4: U1.GPIO32, A6.DIR-(DIR)
  N5: U1.GPIO33, A8.DIR-(DIR)
  N6: U1.GPIO25, A9.DIR-(DIR)
  N7: U1.GPIO26, A6.PUL-(PUL)
  N8: U1.GPIO27, A8.PUL-(PUL)
  N9: U1.GPIO14, A9.PUL-(PUL)
  N10: U1.GND, J57.MOUNT, C1.1, C2.1, C3.1, C4.2, C5.2, C6.2
  N11: U1.GPIO13, A9.ENBL-(ENB), J7.pin3, J7.pin_6
  N12: U1.VIN, A8.DIR+(+5V), J3.pin2, J3.pin_5, J5.pin2, J5.pin_5
  N13: U1.GPIO16, S1.Pin_3, C4.1
  N14: U1.GPIO17, S2.Pin_3, C6.1
  N15: U1.GPIO18, S3.Pin_3, C5.1
  N16: U1.GPIO19, IC1.pin6
  N17: U1.GPIO23, Componente1.pin1
  N18: A1.Pin_1, A2.Pin_1, A3.Pin_1, A3.Pin_4, J29.pin1, J29.pin_4
  N19: A1.Pin_3, J33.MOUNT
  N20: A1.Pin_7, J32.MOUNT
  N21: A2.Pin_3, J34.MOUNT
  N22: A2.Pin_7, J31.MOUNT
  N23: A3.Pin_3, J35.MOUNT
  N24: A3.Pin_7, J30.MOUNT
  N25: A6.B-, J54.terminal_1
  N26: A6.B+, J55.terminal_1
  N27: A6.A-, J53.terminal_1
  N28: A6.A+, J52.terminal_1
  N29: A6.VDC, J8.pin3, J8.pin_6
  N30: A6.GND, J56.pin_6
  N31: A6.ENBL-(ENB), J7.pin_5
  N32: A6.ENBL+(+5V), J4.pin_6
  N33: A6.DIR+(+5V), J4.pin2, J4.pin_5, J5.pin3, J5.pin_6
  N34: A6.PUL+(+5V), J4.pin_4
  N35: S1.Pin_1, J16.MOUNT
  N36: S2.Pin_1, J15.MOUNT
  N37: S3.Pin_1, J14.MOUNT
  N38: V2.Pin_2, J29.pin2
  N39: V2.Pin_1, J20.MOUNT
  N40: V3.Pin_2, J6.pin2, J6.pin_5, Boost_Convertor1.Positive_Input
  N41: V3.Pin_1, J21.MOUNT
  N42: V4.Pin_2, J18.pin2, J18.pin_5, A10.Common_Connect
  N43: V4.Pin_1, J22.MOUNT
  N44: M4.pin_1, IC1.pin11
  N45: M4.pin_2, IC1.pin10
  N46: WATER_PUMP1.pin_1, Componente1.pin5, VALVE1.no_name_yet#1
  N47: WATER_PUMP1.pin_2, Componente1.pin4, VALVE1.no_name_yet#2
  N48: IC1.pin3, J26.MOUNT
  N49: IC1.pin4, Boost_Convertor1.Positive_Output
  N50: IC1.pin5, J27.MOUNT
  N51: Componente1.pin2, J6.pin3, J6.pin_6
  N52: Componente1.pin3, J17.MOUNT
  N53: Componente1.pin6, J18.pin3, J18.pin_6
  N54: Componente1.pin7, J19.MOUNT
  N55: M7.A, J52.terminal_2
  N56: M7.C, J53.terminal_2
  N57: M7.B, J55.terminal_2
  N58: M7.D, J54.terminal_2
  N59: A8.B-, J50.terminal_1
  N60: A8.B+, J51.terminal_1
  N61: A8.A-, J49.terminal_1
  N62: A8.A+, J48.terminal_1
  N63: A8.VDC, V5.Pin_2, J8.pin2, J8.pin_5
  N64: A8.GND, V5.Pin_1, J56.pin2, J56.pin_5, J58.MOUNT
  N65: A8.ENBL-(ENB), J7.pin_4
  N66: A8.ENBL+(+5V), J3.pin_6
  N67: A8.PUL+(+5V), J3.pin_4
  N68: M8.A, J48.terminal_2
  N69: M8.C, J49.terminal_2
  N70: M8.B, J51.terminal_2
  N71: M8.D, J50.terminal_2
  N72: A9.B-, J46.terminal_1
  N73: A9.B+, J47.terminal_1
  N74: A9.A-, J45.terminal_1
  N75: A9.A+, J44.terminal_1
  N76: A9.VDC, J8.pin1, J8.pin_4
  N77: A9.GND, J56.pin_4
  N78: A9.ENBL+(+5V), J2.pin_6
  N79: A9.DIR+(+5V), J2.pin2, J2.pin_5, J5.pin1, J5.pin_4
  N80: A9.PUL+(+5V), J2.pin_4
  N81: M9.A, J44.terminal_2
  N82: M9.C, J45.terminal_2
  N83: M9.B, J47.terminal_2
  N84: M9.D, J46.terminal_2
  N85: Boost_Convertor1.Negative_Input, J24.MOUNT
  N86: Boost_Convertor1.Negative_Output, J25.MOUNT
  N87: A10.Green_Connect, J39.MOUNT

notes:
  Fuente 5V
  Fuente 3.3V
  Fuente 12V
  Fuente 48V
  MOTOR 1
  MOTOR 2
  MOTOR 3
  FC1
  FC2
  FC3
  BOMBA NEUMÁTICA
  MOTORREDUCTOR DC CINTA (60RPM)
  WEBCAM USB
  STEP-UP XL6009E1
  E1
  E2
  E3
  MEDICIÓN ANALÓGICA
  ELECTROVÁLVULA
  330 nF

custom parts:
  ESP32-38PinWide: Generic 38-Pin ESP32 with wide format (only access to one side of pins on a breadboard) based on Stephen Lilley's HiLetgo ESP-WROOM-32 ESP32 ESP-32S Development Board.
  AS5600 module: .This module is mainly placed behind the stepper motor to obtain the rotation angle of the stepper motor.
  DM860A Stepper Motor Driver: DM860A is a type of two-phase hybrid stepping motor driver, The drive voltage of which is from 24VDC to 80VDC. It is designed for use with 2-phase hybrid stepper motor of all kinds with 57mm to 110mm outside diameter and less than 8.0A phase current. Mar 2023: Correct pcb layerId as the part won't save correctly in a .fzz file as is.
  water pump/motor: WATER PUMP BY ARDUBLOCKTR
  DRV8833 Motor Driver Board (MJKDZ): A module made by MJKDZ, containg DRV8833 motor driver chip on PCB with 12-pin DIP 600mil footprint. Contains decoupling caps and an enable pad (J2). Does not bring out all IC pins. EEP = SLEEP input (needs pulling logic high to enable motors) ULT = FAULT output.
  Boost Convertor: DC to DC boost convertor
  RGB Strip LED: A tri-color Strip LED with red, green and blue. Pin order: red - common cathode - blue - green
